# Fritzing sketch E050_COLOR_LED_Control (saved by Fritzing 0.9.3b)
breadboards: 1

parts:
  부품1 = Arduino Uno (Rev3)
  LED1 = RGB LED (com. cathode, rgb) [package="5 mm [THT]"]
  R1 = Resistor [tolerance=±5% resistance=220 package=THT]
  R2 = Resistor [tolerance=±5% resistance=220 package=THT]
  R3 = Resistor [tolerance=±5% resistance=220 package=THT]
  BT1 = Bluetooth HC-06u [package=THT]

nets:
  N1: 부품1.D9_PWM, R3.Pin_0
  N2: 부품1.D10_PWM/SS, R2.Pin_0
  N3: 부품1.D11_PWM/MOSI, R1.Pin_0
  N4: 부품1.D2, BT1.TXD
  N5: 부품1.D3_PWM, BT1.RXD
  5V: 부품1.5V, BT1.VCC
  GND: 부품1.GND, LED1.green_anode, BT1.GND
  N6: LED1.red_anode, R1.Pin_1
  N7: LED1.common_cathode, R2.Pin_1
  N8: LED1.blue_anode, R3.Pin_1

custom parts:
  Bluetooth HC-06u: Bluetooth HC-06 - face up, pins down 16.5mm x 37.5mm PCB
